// Logisim project common_bus.circ as structural Verilog: 1 circuit, main circuit main
module main (
);

  wire clock_1_out, multiplexer_1_out, multiplexer_2_out, multiplexer_3_out, multiplexer_4_out;
  wire [3:0] dipswitch_1_p1, dipswitch_2_p1, dipswitch_3_p2, dipswitch_4_p1, register_1_q, register_2_q,
       register_3_q, register_4_q;

  // DipSwitch dipswitch_1: pin names not known; wires that end beside it: dipswitch_1_p1[0], dipswitch_1_p1[1], dipswitch_1_p1[2], dipswitch_1_p1[3]
  Multiplexer #(.select(2)) multiplexer_1 (
    .in0(register_1_q[3]), .in1(register_2_q[3]), .in2(register_3_q[3]), .in3(register_4_q[3]),
    .out(multiplexer_1_out), .sel(2'b11));
  Register #(.width(4)) register_1 (.D(dipswitch_1_p1), .clk(clock_1_out), .Q(register_1_q));  // open: en, clr
  Clock clock_1 (.out(clock_1_out));
  // DipSwitch dipswitch_2: pin names not known; wires that end beside it: dipswitch_2_p1[0], dipswitch_2_p1[1], dipswitch_2_p1[2], dipswitch_2_p1[3]
  LED led_1 (.in(multiplexer_1_out));
  Register #(.width(4)) register_2 (.D(dipswitch_2_p1), .clk(clock_1_out), .Q(register_2_q));  // open: en, clr
  LED led_2 (.in(multiplexer_2_out));
  Multiplexer #(.select(2)) multiplexer_2 (
    .in0(register_1_q[2]), .in1(register_2_q[2]), .in2(register_3_q[2]), .in3(register_4_q[2]),
    .out(multiplexer_2_out), .sel(2'b11));
  Register #(.width(4)) register_3 (.D(dipswitch_3_p2), .clk(clock_1_out), .Q(register_3_q));  // open: en, clr
  LED led_3 (.in(multiplexer_3_out));
  Multiplexer #(.select(2)) multiplexer_3 (
    .in0(register_1_q[1]), .in1(register_2_q[1]), .in2(register_3_q[1]), .in3(register_4_q[1]),
    .out(multiplexer_3_out), .sel(2'b11));
  Register #(.width(4)) register_4 (.D(dipswitch_4_p1), .clk(clock_1_out), .Q(register_4_q));  // open: en, clr
  // DipSwitch dipswitch_3: pin names not known; wires that end beside it: register_3_q, dipswitch_3_p2[0], dipswitch_3_p2[1], dipswitch_3_p2[2], dipswitch_3_p2[3]
  LED led_4 (.in(multiplexer_4_out));
  Multiplexer #(.select(2)) multiplexer_4 (
    .in0(register_1_q[0]), .in1(register_2_q[0]), .in2(register_3_q[0]), .in3(register_4_q[0]),
    .out(multiplexer_4_out), .sel(2'b11));
  // DipSwitch dipswitch_4: pin names not known; wires that end beside it: dipswitch_4_p1[0], dipswitch_4_p1[1], dipswitch_4_p1[2], dipswitch_4_p1[3]
endmodule
